# Fritzing sketch YASL (saved by Fritzing 0.9.3b)

parts:
  WeMos_D1_Mini1 = WeMos D1 Mini
  IR1 = TSOP312.., 314.. [package=THT]
  MAX4466_Breakout = Breakout Board for Electret Microphone
  U3 = WS2812 RGB LED strip
  U1 = WS2812 RGB LED strip
  U2 = WS2812 RGB LED strip

nets:
  3V3: WeMos_D1_Mini1.3V3, IR1.Vs, MAX4466_Breakout.VCC
  5V: WeMos_D1_Mini1.5V, U1.VCC
  N1: WeMos_D1_Mini1.A0, MAX4466_Breakout.AUD
  N2: WeMos_D1_Mini1.D1, IR1.Data
  N3: WeMos_D1_Mini1.D5, U3.DIN
  GND: WeMos_D1_Mini1.G, IR1.GND, MAX4466_Breakout.GND, U3.GND, U1.GND
  N4: U1.DIN, U2.DIN

notes:
  Status (1-3)
  Effect (2 x 15) in paralell
  TSOP 4838
  MIC
  YASL, YASL Controller Wiring,   1

custom parts:
  WS2812 RGB LED strip: WS2812 strip
